# Fritzing sketch terminal (saved by Fritzing 1.0.2b)

parts:
  LED1 = RGB LED (com. cathode, rgb) [color="Red (633nm)" current=0.030A package="5 mm [THT]"]
  U1 = LCD-16X2 [package=lcd-16x2]
  Componente2 = RFID USB Reader
  Componente3 = Arduino Mega 2560 (Rev3)
  LCM1602_IIC2 = LCM1602 IIC [part_number="LCM1602 IIC" chip_label="LCM1602 IIC" package="DIP (Dual Inline) [THT]"]

nets:
  N1: LED1.red_anode, Componente3.D13_PWM
  5V: LED1.common_cathode, Componente3.5V, LCM1602_IIC2.VCC
  N2: LED1.green_anode, Componente3.D11_PWM
  VSS: U1.VSS, LCM1602_IIC2.VSS
  VDD: U1.VDD, LCM1602_IIC2.VDD
  N3: U1.VO, LCM1602_IIC2.V0
  N4: U1.RS, LCM1602_IIC2.RS
  N5: U1.R_W, LCM1602_IIC2.RW
  N6: U1.E, LCM1602_IIC2.E
  N7: U1.DB0, LCM1602_IIC2.D0
  N8: U1.DB1, LCM1602_IIC2.D1
  N9: U1.DB2, LCM1602_IIC2.D2
  N10: U1.DB3, LCM1602_IIC2.D3
  N11: U1.DB4, LCM1602_IIC2.D4
  N12: U1.DB5, LCM1602_IIC2.D5
  N13: U1.DB6, LCM1602_IIC2.D6
  N14: U1.DB7, LCM1602_IIC2.D7
  N15: U1.A, LCM1602_IIC2.A
  N16: U1.K, LCM1602_IIC2.K
  N17: Componente2.GNDT, Componente3.D51
  N18: Componente2.CP, Componente3.D50
  N19: Componente2.ANT2, Componente3.D49
  N20: Componente2.ANT1, Componente3.D48
  GND: Componente2.TX-O, Componente3.GND, LCM1602_IIC2.GND
  N21: Componente2.GND, Componente3.D5_PWM
  VCC: Componente2.VCC, Componente3.3V3
  N22: Componente3.D21/SCL, LCM1602_IIC2.SCL
  N23: Componente3.D20/SDA, LCM1602_IIC2.SDA
  N24: LCM1602_IIC2.LED_A, LCM1602_IIC2.LED_B

custom parts:
  LCM1602 IIC: I2C-Module to use a 1602 or 2004 LCD on with the wire.h libory Serial LCD Modul
